# Fritzing sketch main (saved by Fritzing 0.9.3b)
circuit board: 8.52876cm x 5.6388cm
breadboards: 1

parts:
  U1 = atmega328 [package=dip]
  XTAL1 = Crystal [frequency="16 Mhz" package=THT]
  IC1 = IC, DIP package, 20 pins [chip_label=74LVC244]
  Raspberry_Pi_2 = Raspberry Pi 2
  C4 = Ceramic Capacitor [capacitance=100nF package="100 mil [THT, multilayer]"]
  C3 = Ceramic Capacitor [capacitance=100nF package="100 mil [THT, multilayer]"]
  R1 = Resistor [tolerance=±5% resistance=10k package=THT]
  R3 = Resistor [tolerance=±5% resistance=10k package=THT]
  R2 = Resistor [tolerance=±5% resistance=100k package=THT]
  C1 = Ceramic Capacitor [capacitance=22pF package="100 mil [THT, multilayer]"]
  C2 = Ceramic Capacitor [capacitance=22pF package="100 mil [THT, multilayer]"]
  R4 = Resistor [tolerance=±5% resistance=10k package=THT]
  R5 = Resistor [tolerance=±5% resistance=10k package=THT]
  R6 = Resistor [tolerance=±5% resistance=10k package=THT]
  R7 = Resistor [tolerance=±5% resistance=10k package=THT]
  M2 = male pin header, 2 pins [form="♂ (male)"]
  M3 = male pin header, 2 pins [form="♂ (male)"]
  M4 = male pin header, 2 pins [form="♂ (male)"]
  M1 = male pin header, 2 pins [form="♂ (male)"]
  A2 = male pin header, 3 pins [form="♂ (male)"]
  A1 = male pin header, 3 pins [form="♂ (male)"]
  A0 = male pin header, 3 pins [form="♂ (male)"]
  Disp = male pin header, 3 pins [form="♂ (male)"]
  Q2 = MOSFET-NCHANNEL [package=to-92]
  Q3 = MOSFET-NCHANNEL [package=to-92]
  Q1 = MOSFET-NCHANNEL [package=to-92]
  GPS = mystery part, 9 pins [chip_label=GPS]
  REG1 = mystery part, 4 pins [chip_label="5V CRIT" part_number=D24V5F5]
  REG2 = mystery part, 4 pins [chip_label=3.3V part_number=D24V5F3]
  Q5 = MOSFET-NCHANNEL [package=to-92]
  R8 = Resistor [tolerance=±5% resistance=100k package=THT]
  PWR = Screw terminal - 2 pins [package=THT]
  R9 = Resistor [tolerance=±5% resistance=100k package=THT]
  R10 = Resistor [tolerance=±5% resistance=100k package=THT]
  Q4 = MOSFET-NCHANNEL [package=to-92]
  REG3 = mystery part, 5 pins [chip_label=5V part_number=D24V22F5]
  Port_1 = Interconnect Port [form="♂ (shrouded male)" package=THT]
  Port_2 = Interconnect Port [form="♂ (shrouded male)" package=THT]
  Port_3 = Interconnect Port [form="♂ (shrouded male)" package=THT]
  Port_4 = Interconnect Port [form="♂ (shrouded male)" package=THT]

nets:
  AVR_RST: U1.RESET, R3.Pin_1, Q1.D
  SHDN: U1.D0_(RX), Q5.G
  PG: U1.D1_(TX), Q4.S
  AVR_D2: U1.D2, M1.pin1
  PWM0: U1.D3_(PWM), M1.pin2
  AVR_D4: U1.D4, M2.pin1
  5V CRIT: U1.VCC, U1.AVCC, C4.0, C3.1, R3.Pin_0, REG1.pin4, Port_1.5V_CRIT, Port_2.5V_CRIT, Port_3.5V_CRIT, Port_4.5V_CRIT
  GND: U1.GND, IC1.pin10, IC1.pin11, IC1.pin13, IC1.pin15, IC1.pin17, Raspberry_Pi_2.GND, C4.1, C3.0, R2.Pin_0, C1.1, C2.1, A2.pin3, A1.pin3, A0.pin3, Disp.pin3, Q1.S, GPS.pin7, REG1.pin3, REG2.pin3, R8.Pin_1, PWR.pin2, R10.Pin_0, REG3.pin4, Port_1.GND, Port_2.GND, Port_3.GND, Port_4.GND
  N1: U1.XLAT1, XTAL1.pin_1, C2.0
  N2: U1.XLAT2, XTAL1.pin_0, C1.0
  PWM1: U1.D5_(PWM), M2.pin2
  PWM2: U1.D6_(PWM), M3.pin2
  AVR_D7: U1.D7, M3.pin1
  AVR_D8: U1.D8, M4.pin1
  PWM3: U1.D9_(PWM), M4.pin2
  N3: U1.D10_(PWM), Disp.pin1
  AVR_MOSI: U1.D11_(PWM), IC1.pin14
  AVR_MISO: U1.D12, IC1.pin8
  AVR_SCK: U1.D13, IC1.pin16
  ADC0: U1.A0, A0.pin1
  ADC1: U1.A1, A1.pin1
  ADC2: U1.A2, A2.pin1
  ADC3: U1.A3, R9.Pin_0, R10.Pin_1
  5V_SDA: U1.A4, R7.Pin_0, Q2.D, Port_1.SDA, Port_2.SDA, Port_3.SDA, Port_4.SDA
  5V_SCL: U1.A5, R6.Pin_0, Q3.D, Port_1.SCL, Port_2.SCL, Port_3.SCL, Port_4.SCL
  PI_CE0: IC1.pin1, Raspberry_Pi_2.GPIO8, R1.Pin_0
  PI_SCK: IC1.pin4, Raspberry_Pi_2.GPIO11
  PI_MOSI: IC1.pin6, Raspberry_Pi_2.GPIO10
  PI_MISO: IC1.pin12, Raspberry_Pi_2.GPIO9
  N4: IC1.pin18, R2.Pin_1, Q1.G
  3.3V: IC1.pin19, IC1.pin20, R1.Pin_1, R4.Pin_1, R5.Pin_1, Q2.G, Q3.G, GPS.pin1, REG2.pin4, Port_1.3.3V, Port_2.3.3V, Port_3.3.3V, Port_4.3.3V
  3.3V_SDA: Raspberry_Pi_2.GPIO2, R4.Pin_0, Q2.S
  3.3V_SCL: Raspberry_Pi_2.GPIO3, R5.Pin_0, Q3.S
  N5: Raspberry_Pi_2.GPIO26, GPS.pin2
  N6: Raspberry_Pi_2.GPIO15, GPS.pin5
  N7: Raspberry_Pi_2.GPIO14, GPS.pin6
  5V: Raspberry_Pi_2.5V, R6.Pin_1, R7.Pin_1, A2.pin2, A1.pin2, A0.pin2, Disp.pin2, REG2.pin2, Q4.D, REG3.pin5, Port_1.5V, Port_2.5V, Port_3.5V, Port_4.5V
  VIN: REG1.pin2, PWR.pin1, R9.Pin_1, REG3.pin3
  N8: Q5.D, REG3.pin2
  N9: Q5.S, R8.Pin_0
  N10: Q4.G, REG3.pin1

notes:
  I2C Level Shifter
  Raspberry Pi Header
  Atmel ATMEGA 328p
  ATMEGA Programmer
  ADC Header
  Expansion Ports
  Motors
  5V
  G
  A
  Rx
  E
  Pathfinder v2.0
  Frontier Robotics ©2016
  M
  +
  -
  GND
  RX
  TX
  EN
  3.3V
  CRIT
  PG
  VIN

custom parts:
  MOSFET-NCHANNEL: Generic NMOS footprint
  Interconnect Port: 6 pin shrouded header for board interconnection.
