# Fritzing sketch navigator (saved by Fritzing 0.9.2b)
breadboards: 1

parts:
  U1 = atmega328 [package=dip]  # not connected
  Raspberry_Pi_2 = Raspberry Pi 2
  XTAL1 = Crystal [frequency="16 Mhz" package=THT]  # not connected
  IC1 = IC, DIP package, 20 pins [chip_label=74LVC244]  # not connected
  GPS1 = female pin header, 9 pins [form="♀ (female)"]

nets:
  N1: Raspberry_Pi_2.3V3, GPS1.pin1
  GND: Raspberry_Pi_2.GND, GPS1.pin7
  N2: Raspberry_Pi_2.GPIO15, GPS1.pin5
  N3: Raspberry_Pi_2.GPIO14, GPS1.pin6

notes:
  3.3V
  EN
  VBAT
  FIX
  TX
  RX
  GND
  VIN
  PPS
